// Logisim project 4-1 Демультиплексер.circ as structural Verilog: 1 circuit, main circuit main
module main (
  input  A0,
  input  A1,
  input  D,
  output Y0,
  output Y1,
  output Y2,
  output Y3
);

  wire not_1_out, not_2_out;

  not not_1 (not_1_out, A0);
  not not_2 (not_2_out, A1);
  and and_1 (Y0, D, not_2_out, not_1_out);
  and and_2 (Y1, D, A1, not_1_out);
  and and_3 (Y2, D, A0, not_2_out);
  and and_4 (Y3, D, A0, A1);
endmodule
