// Logisim project 4-1 Мультиплексер.circ as structural Verilog: 1 circuit, main circuit main
module main (
  input  D,
  input  C,
  input  B,
  input  A,
  input  S1,
  input  S2,
  output Q
);

  wire and_1_out, and_2_out, and_3_out, and_4_out, not_1_out, not_2_out;

  not not_1 (not_1_out, S1);
  not not_2 (not_2_out, S2);
  and and_1 (and_1_out, D, S1, S2);
  and and_2 (and_2_out, C, not_1_out, S2);
  and and_3 (and_3_out, B, not_2_out, S1);
  and and_4 (and_4_out, A, not_1_out, not_2_out);
  or or_1 (Q, and_1_out, and_2_out, and_3_out, and_4_out);
endmodule
